// Logisim project CPU.circ as structural Verilog: 11 circuits, main circuit main
module main (
  output [9:0] out_1,
  output [9:0] out_2,
  output [9:0] out_3,
  output [9:0] out_4,
  output [9:0] out_5,
  output [9:0] out_6,
  output [9:0] out_7,
  output ignore,
  output halt
);

  wire and_1_out, and_2_out, and_3_out, BNEZ, CLK, clock_1_out, comparator_1_lt, comparator_2_lt, Enable,
       Get_Dest, HALT_t, not_1_out, not_3_out, not_4_out, not_5_out, SEL_A, t_ff_1_q, TClock;
  wire [1:0] counter_2_q, SEL_B, Upper_2_bits;
  wire [2:0] A_address, B_address, Dest_address, rom_1_data, SEL;
  wire [4:0] _5_bit_ALU_c, _5_bit_PC_data_out, counter_1_q, multiplexer_5_out, OpCode;
  wire [6:0] adder_1_out, adder_2_out, ASCII, LSB, MiddleBits;
  wire [7:0] multiplexer_1_out;
  wire [9:0] A, ALU_Out, B, Data, multiplexer_6_out, multiplexer_7_out;

  TTY #(.rows(33), .cols(4)) tty_1 (.data(ASCII), .clk(TClock));  // open: we, clr
  Counter #(.width(5), .max('h1f), .ongoal("stay")) counter_1 (
    .Q(counter_1_q), .carry(halt), .clk(CLK));  // open: load, D, count, clr
  // Probe on out_1
  // Probe on out_5
  Multiplexer #(.select(3), .width(10)) multiplexer_1 (
    .in0(out_1), .in1(out_2), .in2(out_3), .in3(out_4), .in4(out_5), .in5(out_6), .in6(out_7),
    .out({Upper_2_bits, multiplexer_1_out}), .sel(rom_1_data));  // open: in7, en
  not not_1 (not_1_out, halt);
  Clock clock_1 (.out(clock_1_out));
  // Probe on out_2
  // Probe on out_6
  and and_1 (and_1_out, not_1_out, clock_1_out);
  // Probe on out_3
  // Probe on out_7
  ROM #(.addrWidth(5), .dataWidth(3)) rom_1 (.addr(counter_1_q), .data(rom_1_data));  // open: sel
  not not_2 (TClock, and_1_out);
  // Probe on out_4
  Comparator #(.width(7)) comparator_1 (
    .a(7'b0111001), .b({3'b011, multiplexer_1_out[3:0]}), .lt(comparator_1_lt));  // open: gt, eq
  Comparator #(.width(7)) comparator_2 (
    .a(7'b0111001), .b({3'b011, multiplexer_1_out[7:4]}), .lt(comparator_2_lt));  // open: gt, eq
  T_Flip_Flop t_ff_1 (.clk(and_1_out), .T(1'b1), .Q(t_ff_1_q));  // open: Qn, preset, reset, en
  Adder #(.width(7)) adder_1 (
    .a({3'b011, multiplexer_1_out[3:0]}), .b(7'b0000111), .out(adder_1_out));  // open: cin, cout
  Adder #(.width(7)) adder_2 (
    .a({3'b011, multiplexer_1_out[7:4]}), .b(7'b0000111), .out(adder_2_out));  // open: cin, cout
  Multiplexer #(.select(2), .width(7)) multiplexer_2 (
    .in0({5'b01100, Upper_2_bits}), .in1(MiddleBits), .in2(LSB), .in3(7'b0100000), .out(ASCII),
    .sel(counter_2_q));  // open: en
  Counter #(.width(2), .max('h3)) counter_2 (.Q(counter_2_q), .clk(TClock));  // open: load, D, count, carry, clr
  T_Flip_Flop t_ff_2 (.clk(t_ff_1_q), .T(1'b1), .Q(CLK));  // open: Qn, preset, reset, en
  Multiplexer #(.width(7), .disabled(0), .enable("false")) multiplexer_3 (
    .in0({3'b011, multiplexer_1_out[3:0]}), .in1(adder_1_out), .out(LSB), .sel(comparator_1_lt));
  Multiplexer #(.width(7), .disabled(0), .enable("false")) multiplexer_4 (
    .in0({3'b011, multiplexer_1_out[7:4]}), .in1(adder_2_out), .out(MiddleBits), .sel(comparator_2_lt));
  T_Flip_Flop t_ff_3 (.clk(CLK), .T(1'b1), .Q(ignore));  // open: Qn, preset, reset, en
  not not_3 (not_3_out, CLK);
  not not_4 (not_4_out, HALT_t);
  and and_2 (and_2_out, not_3_out, not_4_out);
  _5_bit_ALU _5_bit_ALU (.A(_5_bit_PC_data_out), .B(multiplexer_5_out), .C(_5_bit_ALU_c));
  _5_bit_Program_Counter _5_bit_PC (.Data_In(_5_bit_ALU_c), .Data_Out(_5_bit_PC_data_out), .CLK(and_2_out));
  and and_3 (and_3_out, CLK, not_5_out);
  not not_5 (not_5_out, HALT_t);
  RAM #(.addrWidth(5), .dataWidth(24)) ram_1 (
    .addr(_5_bit_PC_data_out), .data({OpCode, Dest_address, A_address, B_address, Data}), .clk(and_3_out));  // open: sel, ld, clr
  Multiplexer #(.width(5)) multiplexer_5 (
    .in0(5'b00001), .in1(Data[4:0]), .out(multiplexer_5_out), .sel(BNEZ));  // open: en
  Control_Unit Control_Unit (
    .OPCode(OpCode), .Sel(SEL), .A_Sel(SEL_A), .HALT(HALT_t), .Enable(Enable), .Get_Dest(Get_Dest),
    .B_Sel(SEL_B), .ALU_Out(ALU_Out), .BNEZ(BNEZ));
  Multiplexer #(.width(10)) multiplexer_6 (.in0(Data), .in1(A), .out(multiplexer_6_out), .sel(SEL_A));  // open: en
  ALU alu_1 (.SEL(SEL), .A(multiplexer_6_out), .B(multiplexer_7_out), .C(ALU_Out));
  Multiplexer #(.select(2), .width(10)) multiplexer_7 (
    .in0(Data), .in1(B), .in2({10{1'b0}}), .out(multiplexer_7_out), .sel(SEL_B));  // open: in3, en
  Register_Bank Register_bank (
    .Input_Data(ALU_Out), .Load_from_Input(Enable), .A_output(A), .B_output(B), .Dest(Dest_address),
    .CLK(CLK), .R0(out_1), .R1(out_2), .R2(out_3), .R3(out_4), .R4(out_5), .R5(out_6), .R6(out_7),
    .A_Address(A_address), .B_Address(B_address), .Get_Dest(Get_Dest));

  // Other names for the same wires on the sheet: R0[9:0] = out_1; R1[9:0] = out_2; R2[9:0] = out_3; R3[9:0] = out_4;
  //   R4[9:0] = out_5; R5[9:0] = out_6; R6[9:0] = out_7

  // Notes on the sheet:
  //   DO NOT PUT ANY PINS ON THE main circuit.  (You should not need any anyway.)
  //   0F5
  //   0F5
  //   25A
  //   050
  //   2FF
  //   30A
  //   34F
  //   0F5
  //   1EA
  //   07A
  //   29B
  //   165
  //   10F
  //   0F5
  //   0AA
  //   0AA
  //   05A
  //   00A
  //   0FA
  //   104
  //   0B4
  //   165
  //   165
  //   001
  //   001
  //   000
  //   000
  //   000
  //   000
  //   000
  //   ???
  //   There is no Reset.  Just Ctrl-r, then load test.txt into your RAM, and then Ctrl-k
  //   You must  use the CLK tunnel for the source of your clock.  R0-R6 are the other tunnels you need to connect
  //   contents of rom_1 (hex, n*v repeats v):
  //   0 0 0 1 2 3 4 5 6 2 3 4 5 6 0 0 0 1 3 4 6 3 5 5 8*6
endmodule

module Register_Bank (
  input  [9:0] Input_Data,
  input  Load_from_Input,
  input  Get_Dest,
  input  [2:0] A_Address,
  input  [2:0] B_Address,
  input  [2:0] Dest,
  input  CLK,
  output [9:0] R0,
  output [9:0] A_output,
  output [9:0] R1,
  output [9:0] R2,
  output [9:0] R3,
  output [9:0] B_output,
  output [9:0] R4,
  output [9:0] R5,
  output [9:0] R6
);

  wire and_1_out, and_2_out, and_3_out, and_4_out, and_5_out, and_6_out, and_7_out, decoder_1_out0,
       decoder_1_out1, decoder_1_out2, decoder_1_out3, decoder_1_out4, decoder_1_out5, decoder_1_out6;
  wire [2:0] multiplexer_3_out;

  Decoder #(.select(3)) decoder_1 (
    .out0(decoder_1_out0), .out1(decoder_1_out1), .out2(decoder_1_out2), .out3(decoder_1_out3),
    .out4(decoder_1_out4), .out5(decoder_1_out5), .out6(decoder_1_out6), .sel(Dest));  // open: out7, en
  and and_1 (and_1_out, Load_from_Input, decoder_1_out0);
  and and_2 (and_2_out, Load_from_Input, decoder_1_out1);
  and and_3 (and_3_out, Load_from_Input, decoder_1_out2);
  and and_4 (and_4_out, Load_from_Input, decoder_1_out3);
  and and_5 (and_5_out, Load_from_Input, decoder_1_out4);
  and and_6 (and_6_out, Load_from_Input, decoder_1_out5);
  and and_7 (and_7_out, Load_from_Input, decoder_1_out6);
  Register u_R0 (.Data_In(Input_Data), .Load(and_1_out), .Clock(CLK), .Data_Out(R0));
  Register u_R1 (.Data_In(Input_Data), .Load(and_2_out), .Clock(CLK), .Data_Out(R1));
  Register u_R2 (.Data_In(Input_Data), .Load(and_3_out), .Clock(CLK), .Data_Out(R2));
  Register u_R3 (.Data_In(Input_Data), .Load(and_4_out), .Clock(CLK), .Data_Out(R3));
  Register u_R4 (.Data_In(Input_Data), .Load(and_5_out), .Clock(CLK), .Data_Out(R4));
  Register u_R5 (.Data_In(Input_Data), .Load(and_6_out), .Clock(CLK), .Data_Out(R5));
  Register u_R6 (.Data_In(Input_Data), .Load(and_7_out), .Clock(CLK), .Data_Out(R6));
  Multiplexer #(.select(3), .width(10)) multiplexer_1 (
    .in0(R0), .in1(R1), .in2(R2), .in3(R3), .in4(R4), .in5(R5), .in6(R6), .out(A_output),
    .sel(multiplexer_3_out));  // open: in7, en
  Multiplexer #(.select(3), .width(10)) multiplexer_2 (
    .in0(R0), .in1(R1), .in2(R2), .in3(R3), .in4(R4), .in5(R5), .in6(R6), .out(B_output), .sel(B_Address));  // open: in7, en
  Multiplexer #(.width(3)) multiplexer_3 (
    .in0(A_Address), .in1(Dest), .out(multiplexer_3_out), .sel(Get_Dest));  // open: en
endmodule

module Register (
  input  [9:0] Data_In,
  input  Load,
  input  Clock,
  output [9:0] Data_Out
);

  wire and_1_out;

  and and_1 (and_1_out, Load, Clock);
  D_Flip_Flop _0 (.clk(and_1_out), .D(Data_In[0]), .Q(Data_Out[0]));  // open: Qn, preset, en, reset
  D_Flip_Flop _5 (.clk(and_1_out), .D(Data_In[5]), .Q(Data_Out[5]));  // open: Qn, preset, en, reset
  D_Flip_Flop _1 (.clk(and_1_out), .D(Data_In[1]), .Q(Data_Out[1]));  // open: Qn, preset, en, reset
  D_Flip_Flop _6 (.clk(and_1_out), .D(Data_In[6]), .Q(Data_Out[6]));  // open: Qn, preset, en, reset
  D_Flip_Flop _2 (.clk(and_1_out), .D(Data_In[2]), .Q(Data_Out[2]));  // open: Qn, preset, en, reset
  D_Flip_Flop _7 (.clk(and_1_out), .D(Data_In[7]), .Q(Data_Out[7]));  // open: Qn, preset, en, reset
  D_Flip_Flop _3 (.clk(and_1_out), .D(Data_In[3]), .Q(Data_Out[3]));  // open: Qn, preset, en, reset
  D_Flip_Flop _8 (.clk(and_1_out), .D(Data_In[8]), .Q(Data_Out[8]));  // open: Qn, preset, en, reset
  D_Flip_Flop _4 (.clk(and_1_out), .D(Data_In[4]), .Q(Data_Out[4]));  // open: Qn, preset, en, reset
  D_Flip_Flop _9 (.clk(and_1_out), .D(Data_In[9]), .Q(Data_Out[9]));  // open: Qn, preset, en, reset
endmodule

module ALU (
  input  [2:0] SEL,
  input  [9:0] A,
  input  [9:0] B,
  output [9:0] C
);

  wire CIN, CIN1, CIN2, CIN3, CIN4, CIN5, CIN6, CIN7, CIN8, CIN9, COUT9, G0, G1, G2, G3, G4, G5, G6, G7, G8,
       G9, P0, P1, P2, P3, P4, P5, P6, P7, P8, P9, SEL_nB;

  // Probe on SEL
  and _111 (SEL_nB, SEL[0], SEL[1], SEL[2]);
  BitALU ALU0 (.A(A[0]), .B(B[0]), .CIN(CIN), .A_right(1'b0), .A_left(A[1]), .P(P0), .G(G0), .C(C[0]), .SEL(SEL));
  BitALU ALU1 (.A(A[1]), .B(B[1]), .CIN(CIN1), .A_right(A[0]), .A_left(A[2]), .P(P1), .G(G1), .C(C[1]), .SEL(SEL));
  BitALU ALU2 (.A(A[2]), .B(B[2]), .CIN(CIN2), .A_right(A[1]), .A_left(A[3]), .P(P2), .G(G2), .C(C[2]), .SEL(SEL));
  BitALU ALU3 (.A(A[3]), .B(B[3]), .CIN(CIN3), .A_right(A[2]), .A_left(A[4]), .P(P3), .G(G3), .C(C[3]), .SEL(SEL));
  BitALU ALU4 (.A(A[4]), .B(B[4]), .CIN(CIN4), .A_right(A[3]), .A_left(A[5]), .P(P4), .G(G4), .C(C[4]), .SEL(SEL));
  Multiplexer multiplexer_1 (.in0(1'b0), .in1(1'b1), .out(CIN), .sel(SEL_nB));  // open: en
  BitALU ALU5 (.A(A[5]), .B(B[5]), .CIN(CIN5), .A_right(A[4]), .A_left(A[6]), .P(P5), .G(G5), .C(C[5]), .SEL(SEL));
  BitALU ALU6 (.A(A[6]), .B(B[6]), .CIN(CIN6), .A_right(A[5]), .A_left(A[7]), .P(P6), .G(G6), .C(C[6]), .SEL(SEL));
  BitALU ALU7 (.A(A[7]), .B(B[7]), .CIN(CIN7), .A_right(A[6]), .A_left(A[8]), .P(P7), .G(G7), .C(C[7]), .SEL(SEL));
  BitALU ALU8 (.A(A[8]), .B(B[8]), .CIN(CIN8), .A_right(A[7]), .A_left(A[9]), .P(P8), .G(G8), .C(C[8]), .SEL(SEL));
  BitALU ALU9 (.A(A[9]), .B(B[9]), .CIN(CIN9), .A_right(A[8]), .A_left(1'b0), .P(P9), .G(G9), .C(C[9]), .SEL(SEL));
  CLA cla_1 (
    .Cout0(CIN1), .Cout5(CIN6), .Cout1(CIN2), .Cout6(CIN7), .Cout2(CIN3), .Cout7(CIN8), .Cout3(CIN4),
    .Cout8(CIN9), .Cout4(CIN5), .Cout9(COUT9), .CIN(CIN), .G0(G0), .P0(P0), .G1(G1), .P1(P1), .G2(G2),
    .P2(P2), .G3(G3), .P3(P3), .G4(G4), .P4(P4), .G5(G5), .P5(P5), .G6(G6), .P6(P6), .G7(G7), .P7(P7),
    .G8(G8), .P8(P8), .G9(G9), .P9(P9));

  // Other names for the same wires on the sheet: SEL1[2:0] = SEL
endmodule

module BitALU (
  input  A,
  input  B,
  input  [2:0] SEL,
  input  CIN,
  input  A_right,
  input  A_left,
  output P,
  output G,
  output C
);

  wire multiplexer_1_out, not_1_out, not_2_out, SEL_nB, xor_1_out, xor_2_out;

  not not_1 (not_1_out, B);
  Multiplexer multiplexer_1 (.in0(B), .in1(not_1_out), .out(multiplexer_1_out), .sel(SEL_nB));  // open: en
  and and_1 (G, A, multiplexer_1_out);
  or or_1 (P, A, multiplexer_1_out);
  not not_2 (not_2_out, A);
  xor xor_1 (xor_1_out, multiplexer_1_out, A);
  xor xor_2 (xor_2_out, xor_1_out, CIN);
  Multiplexer #(.select(3), .enable("false")) multiplexer_2 (
    .in0(G), .in1(P), .in2(not_2_out), .in3(xor_2_out), .in4(A), .in5(A_right), .in6(A_left),
    .in7(xor_2_out), .out(C), .sel(SEL));
  and _111 (SEL_nB, SEL[0], SEL[1], SEL[2]);
endmodule

module CLA (
  input  CIN,
  input  G0,
  input  P0,
  input  G1,
  input  P1,
  input  G2,
  input  P2,
  input  G3,
  input  P3,
  input  G4,
  input  P4,
  input  G5,
  input  P5,
  input  G6,
  input  P6,
  input  G7,
  input  P7,
  input  G8,
  input  P8,
  input  G9,
  input  P9,
  output Cout0,
  output Cout5,
  output Cout1,
  output Cout6,
  output Cout2,
  output Cout7,
  output Cout3,
  output Cout8,
  output Cout4,
  output Cout9
);

  wire P0CIN_2_out, P0CIN_out, P01CIN_2_out, P01CIN_out, P1G0_2_out, P1G0_out, P2G1_2_out, P2G1_out,
       P3G2_2_out, P3G2_out, P4G3_2_out, P4G3_out, P012CIN_2_out, P012CIN_out, P12G0_2_out, P12G0_out,
       P23G1_2_out, P23G1_out, P34G2_2_out, P34G2_out, P0123CIN_2_out, P0123CIN_out, P123G0_2_out,
       P123G0_out, P234G1_2_out, P234G1_out, P01234CIN_2_out, P01234CIN_out, P1234G0_2_out, P1234G0_out;

  and P0CIN (P0CIN_out, P0, CIN);
  and P1G0 (P1G0_out, P1, G0);
  and P01CIN (P01CIN_out, P0, P1, CIN);
  and P2G1 (P2G1_out, P2, G1);
  and P12G0 (P12G0_out, P1, P2, G0);
  and P012CIN (P012CIN_out, P0, P1, P2, CIN);
  and P3G2 (P3G2_out, P3, G2);
  and P23G1 (P23G1_out, P2, P3, G1);
  and P123G0 (P123G0_out, P1, P2, P3, G0);
  and P0123CIN (P0123CIN_out, P0, P1, P2, P3, CIN);
  and P4G3 (P4G3_out, P4, G3);
  and P34G2 (P34G2_out, P3, P4, G2);
  and P234G1 (P234G1_out, P2, P3, P4, G1);
  and P1234G0 (P1234G0_out, P1, P2, P3, P4, G0);
  and P01234CIN (P01234CIN_out, P0, P1, P2, P3, P4, CIN);
  or or_1 (Cout0, P0CIN_out, G0);
  or or_2 (Cout1, P1G0_out, P01CIN_out, G1);
  or or_3 (Cout2, P2G1_out, P12G0_out, P012CIN_out, G2);
  or or_4 (Cout3, P3G2_out, P23G1_out, P123G0_out, P0123CIN_out, G3);
  or or_5 (Cout4, P4G3_out, P34G2_out, P234G1_out, P1234G0_out, P01234CIN_out, G4);
  and P0CIN_2 (P0CIN_2_out, P5, Cout4);
  and P1G0_2 (P1G0_2_out, P6, G5);
  and P01CIN_2 (P01CIN_2_out, P5, P6, Cout4);
  and P2G1_2 (P2G1_2_out, P7, G6);
  and P12G0_2 (P12G0_2_out, P6, P7, G5);
  and P012CIN_2 (P012CIN_2_out, P5, P6, P7, Cout4);
  and P3G2_2 (P3G2_2_out, P8, G7);
  and P23G1_2 (P23G1_2_out, P7, P8, G6);
  and P123G0_2 (P123G0_2_out, P6, P7, P8, G5);
  and P0123CIN_2 (P0123CIN_2_out, P5, P6, P7, P8, Cout4);
  and P4G3_2 (P4G3_2_out, P9, G8);
  and P34G2_2 (P34G2_2_out, P8, P9, G7);
  and P234G1_2 (P234G1_2_out, P7, P8, P9, G6);
  and P1234G0_2 (P1234G0_2_out, P6, P7, P8, P9, G5);
  and P01234CIN_2 (P01234CIN_2_out, P5, P6, P7, P8, P9, Cout4);
  or or_6 (Cout5, P0CIN_2_out, G5);
  or or_7 (Cout6, P1G0_2_out, P01CIN_2_out, G6);
  or or_8 (Cout7, P2G1_2_out, P12G0_2_out, P012CIN_2_out, G7);
  or or_9 (Cout8, P3G2_2_out, P23G1_2_out, P123G0_2_out, P0123CIN_2_out, G8);
  or or_10 (Cout9, P4G3_2_out, P34G2_2_out, P234G1_2_out, P1234G0_2_out, P01234CIN_2_out, G9);

  // Other names for the same wires on the sheet: C4 = Cout4
endmodule

module Control_Unit (
  input  [4:0] OPCode,
  input  [9:0] ALU_Out,
  output [2:0] Sel,
  output A_Sel,
  output [1:0] B_Sel,
  output Get_Dest,
  output BNEZ,
  output Enable,
  output HALT
);

  wire nand_1_out, NOP_out, not_1_out, not_2_out, not_3_out, not_4_out, not_5_out, or_1_out, or_2_out;
  wire [1:0] not_9_out;
  wire [2:2] not_7_out;

  not not_1 (not_1_out, OPCode[4]);
  not not_2 (not_2_out, OPCode[1]);
  not not_3 (not_3_out, OPCode[3]);
  not not_4 (not_4_out, OPCode[0]);
  not not_5 (not_5_out, OPCode[2]);
  and and_1 (B_Sel[0], not_1_out, not_3_out);
  and u_BNEZ (B_Sel[1], not_1_out, OPCode[3], not_5_out, OPCode[1], OPCode[0]);
  and NOP (NOP_out, not_1_out, OPCode[3], OPCode[2], not_2_out, not_4_out);
  and u_HALT (HALT, OPCode[4], OPCode[3], OPCode[2], OPCode[1], OPCode[0]);
  nand nand_1 (nand_1_out, not_1_out, OPCode[3], not_5_out, OPCode[1], not_4_out);
  or or_1 (or_1_out, B_Sel[1], NOP_out, HALT);
  buf and_2 (A_Sel, nand_1_out);  // AND_Gate
  not not_6 (Enable, or_1_out);
  or or_2 (or_2_out, ALU_Out[0], ALU_Out[1], ALU_Out[2], ALU_Out[3], ALU_Out[4], ALU_Out[5], ALU_Out[6], ALU_Out[7], ALU_Out[8], ALU_Out[9]);
  not not_7 (not_7_out[2], 1'b1);
  not not_8 (not_9_out[1], 1'b1);
  and and_3 (BNEZ, B_Sel[1], or_2_out);
  not not_9 (not_9_out[0], 1'b1);
  Multiplexer #(.select(4), .width(3)) multiplexer_1 (
    .in0(OPCode[2:0]), .in1(OPCode[2:0]), .in2(OPCode[2:0]), .in3(OPCode[2:0]), .in4(OPCode[2:0]),
    .in5(OPCode[2:0]), .in6(OPCode[2:0]), .in7(OPCode[2:0]), .in8({not_7_out[2], 2'b11}), .in9(3'b111),
    .in10({1'b1, not_9_out}), .in11({1'b1, not_9_out[1], not_7_out[2]}), .in12(3'b111), .in13(3'b111),
    .in14(3'b111), .in15(3'b111), .out(Sel), .sel(OPCode[3:0]));  // open: en

  assign Get_Dest = B_Sel[1];

  // Other names for the same wires on the sheet: OPC[3:0] = OPCode[3:0]; S0 = OPCode[0]; S1 = OPCode[1];
  //   S2 = OPCode[2]; en = Enable; S3 = OPCode[3]; S4 = OPCode[4]
endmodule

module _5_bit_Program_Counter (
  input  [4:0] Data_In,
  input  CLK,
  output [4:0] Data_Out
);

  wire and_1_out, undriven, undriven_2;

  and and_1 (and_1_out, undriven, undriven_2);
  D_Flip_Flop _0 (.clk(CLK), .D(Data_In[0]), .Q(Data_Out[0]));  // open: Qn, preset, en, reset
  D_Flip_Flop _1 (.clk(CLK), .D(Data_In[1]), .Q(Data_Out[1]));  // open: Qn, preset, en, reset
  D_Flip_Flop _2 (.clk(CLK), .D(Data_In[2]), .Q(Data_Out[2]));  // open: Qn, preset, en, reset
  D_Flip_Flop _3 (.clk(CLK), .D(Data_In[3]), .Q(Data_Out[3]));  // open: Qn, preset, en, reset
  D_Flip_Flop _4 (.clk(CLK), .D(Data_In[4]), .Q(Data_Out[4]));  // open: Qn, preset, en, reset
endmodule

module _5_bit_ALU (
  input  [4:0] A,
  input  [4:0] B,
  output [4:0] C
);

  wire C5, CIN1, CIN2, CIN3, CIN4, G0, G1, G2, G3, G4, P0, P1, P2, P3, P4;

  _5_bit_BitALU u_5_bit_bitalu_1 (.A(A[0]), .B(B[0]), .CIN(1'b0), .P(P0), .G(G0), .C(C[0]), .SEL(2'b11));
  _5_bit_BitALU u_5_bit_bitalu_2 (.A(A[1]), .B(B[1]), .CIN(CIN1), .P(P1), .G(G1), .C(C[1]), .SEL(2'b11));
  _5_bit_BitALU u_5_bit_bitalu_3 (.A(A[2]), .B(B[2]), .CIN(CIN2), .P(P2), .G(G2), .C(C[2]), .SEL(2'b11));
  _5_bit_BitALU u_5_bit_bitalu_4 (.A(A[3]), .B(B[3]), .CIN(CIN3), .P(P3), .G(G3), .C(C[3]), .SEL(2'b11));
  _5_bit_BitALU u_5_bit_bitalu_5 (.A(A[4]), .B(B[4]), .CIN(CIN4), .P(P4), .G(G4), .C(C[4]), .SEL(2'b11));
  // Probe on 2'b11
  _5_bit_CLA u_5_bit_cla_1 (
    .CIN(1'b0), .G0(G0), .P0(P0), .G1(G1), .P1(P1), .G2(G2), .P2(P2), .G3(G3), .P3(P3), .G4(G4), .P4(P4),
    .Cout0(CIN1), .Cout1(CIN2), .Cout2(CIN3), .Cout3(CIN4), .Cout4(C5));
endmodule

module _5_bit_BitALU (
  input  A,
  input  B,
  input  [1:0] SEL,
  input  CIN,
  output P,
  output G,
  output C
);

  wire not_1_out, xor_1_out, xor_2_out;

  and and_1 (G, A, B);
  or or_1 (P, A, B);
  not not_1 (not_1_out, A);
  xor xor_1 (xor_1_out, B, A);
  xor xor_2 (xor_2_out, xor_1_out, CIN);
  Multiplexer #(.select(2), .enable("false")) multiplexer_1 (
    .in0(G), .in1(P), .in2(not_1_out), .in3(xor_2_out), .out(C), .sel(SEL));
endmodule

module _5_bit_CLA (
  input  CIN,
  input  G0,
  input  P0,
  input  G1,
  input  P1,
  input  G2,
  input  P2,
  input  G3,
  input  P3,
  input  G4,
  input  P4,
  output Cout0,
  output Cout1,
  output Cout2,
  output Cout3,
  output Cout4
);

  wire P0CIN_out, P01CIN_out, P1G0_out, P2G1_out, P3G2_out, P4G3_out, P012CIN_out, P12G0_out, P23G1_out,
       P34G2_out, P0123CIN_out, P123G0_out, P234G1_out, P01234CIN_out, P1234G0_out;

  and P0CIN (P0CIN_out, P0, CIN);
  and P1G0 (P1G0_out, P1, G0);
  and P01CIN (P01CIN_out, P0, P1, CIN);
  and P2G1 (P2G1_out, P2, G1);
  and P12G0 (P12G0_out, P1, P2, G0);
  and P012CIN (P012CIN_out, P0, P1, P2, CIN);
  and P3G2 (P3G2_out, P3, G2);
  and P23G1 (P23G1_out, P2, P3, G1);
  and P123G0 (P123G0_out, P1, P2, P3, G0);
  and P0123CIN (P0123CIN_out, P0, P1, P2, P3, CIN);
  and P4G3 (P4G3_out, P4, G3);
  and P34G2 (P34G2_out, P3, P4, G2);
  and P234G1 (P234G1_out, P2, P3, P4, G1);
  and P1234G0 (P1234G0_out, P1, P2, P3, P4, G0);
  and P01234CIN (P01234CIN_out, P0, P1, P2, P3, P4, CIN);
  or or_1 (Cout0, P0CIN_out, G0);
  or or_2 (Cout1, P1G0_out, P01CIN_out, G1);
  or or_3 (Cout2, P2G1_out, P12G0_out, P012CIN_out, G2);
  or or_4 (Cout3, P3G2_out, P23G1_out, P123G0_out, P0123CIN_out, G3);
  or or_5 (Cout4, P4G3_out, P34G2_out, P234G1_out, P1234G0_out, P01234CIN_out, G4);
endmodule
